# Fritzing sketch StandUp (saved by Fritzing 0.9.1b)
breadboards: 1

parts:
  Part1 = Arduino Uno (Rev3)
  Part2 = JY-MCU HC-06 Bluetooth Module
  J1 = Basic Force Sensing Resistor (FSR) [package=THT]
  R1 = Resistor [tolerance=±5% resistance=330 package=THT]
  LED1 = LED - 5mm [color="Green (555nm)" package="5 mm [THT]"]
  R2 = Resistor [tolerance=±5% resistance=330 package=THT]

nets:
  N1: Part1.A0, J1.pin_1, R1.Pin_1
  N2: Part1.D12/MISO, LED1.anode
  N3: Part1.D0/RX, Part2.TX
  N4: Part1.D1/TX, Part2.RX
  3V3: Part1.3V3, Part2.VCC
  N5: Part1.5V, R1.Pin_0
  GND: Part1.GND, Part2.GND, J1.pin_0, R2.Pin_0
  N6: LED1.cathode, R2.Pin_1

custom parts:
  JY-MCU HC-06 Bluetooth Module: Industrial serial port bluetooth, Drop-in replacement for wired serial connections, transparent usage. You can use it simply for a serial port replacement to establish connection between MCU and GPS, PC to your embedded project and etc. Computer and peripheral devices GPS receiver Industrial control MCU projects Running in slave role: Pair with BT dongle and master module Coupled Mode: Two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
